# Fritzing sketch diagram_LDR (saved by Fritzing 0.9.3b)
breadboards: 1

parts:
  part = Resistor [tolerance=±5% resistance=220 package=THT]
  part_2 = Resistor [tolerance=±5% resistance=220 package=THT]
  R3 = Photocell (LDR) [package=THT]
  Part1 = Arduino Uno (Rev3)
  LED1 = smd LED [color="Red (633nm)" package="1206 [SMD]"]

nets:
  N1: part.Pin_0, part_2.Pin_1, Part1.GND
  N2: part.Pin_1, R3.pin_0, Part1.A0
  N3: part_2.Pin_0, LED1.anode
  N4: R3.pin_1, Part1.5V
  N5: Part1.D3_PWM, LED1.cathode
